// Logisim project 5BitAdder.circ as structural Verilog: 3 circuits, main circuit main
module main (
  input  in_1,
  input  [4:0] in_2,
  input  [4:0] in_3,
  output [4:0] out_4
);

  _5BitAdder u_5bitadder_1 (.Carry_In(in_1), .in_2(in_2), .in_3(in_3), .out_4(out_4));

  // Notes on the sheet:
  //   I CAN'T MAKE THE 5BITADDER BIGGER. PLEASE DON'T DOCK :(
  //   REBEKAH JENSEN
endmodule

module _5BitAdder (
  input  Carry_In,
  input  [4:0] in_2,
  input  [4:0] in_3,
  output [4:0] out_4
);

  wire n1bitadder_1_carry_out, n1bitadder_2_carry_out, n1bitadder_3_carry_out, n1bitadder_4_carry_out;

  _1BitAdder u_1bitadder_1 (
    .A(in_2[0]), .B(in_3[0]), .Carry_In(Carry_In), .C(out_4[0]), .Carry_Out(n1bitadder_1_carry_out));
  _1BitAdder u_1bitadder_2 (
    .A(in_2[1]), .B(in_3[1]), .Carry_In(n1bitadder_1_carry_out), .C(out_4[1]),
    .Carry_Out(n1bitadder_2_carry_out));
  _1BitAdder u_1bitadder_3 (
    .A(in_2[2]), .B(in_3[2]), .Carry_In(n1bitadder_2_carry_out), .C(out_4[2]),
    .Carry_Out(n1bitadder_3_carry_out));
  _1BitAdder u_1bitadder_4 (
    .A(in_2[3]), .B(in_3[3]), .Carry_In(n1bitadder_3_carry_out), .C(out_4[3]),
    .Carry_Out(n1bitadder_4_carry_out));
  _1BitAdder u_1bitadder_5 (
    .A(in_2[4]), .B(in_3[4]), .Carry_In(n1bitadder_4_carry_out), .C(out_4[4]));  // open: Carry_Out
endmodule

module _1BitAdder (
  input  A,
  input  B,
  input  Carry_In,
  output C,
  output Carry_Out
);

  wire and_1_out, and_2_out, xor_1_out;

  xor xor_1 (xor_1_out, A, B);
  xor xor_2 (C, xor_1_out, Carry_In);
  and and_1 (and_1_out, xor_1_out, Carry_In);
  and and_2 (and_2_out, A, B);
  or or_1 (Carry_Out, and_1_out, and_2_out);
endmodule
