// Logisim project AddingCircuitWithDisplay.circ as structural Verilog: 5 circuits, main circuit main
module main (
  input  [4:0] Val,
  input  [4:0] Val_2
);

  wire [6:0] n5bitadderdisplay_1_tens, n5bitadderdisplay_1_tens_2;

  _5BitAdderDisplay u_5bitadderdisplay_1 (
    .Val(Val), .Val_2(Val_2), .Tens(n5bitadderdisplay_1_tens), .Tens_2(n5bitadderdisplay_1_tens_2));
  _7_Segment_Display u_7_segment_display_1 (
    .g(n5bitadderdisplay_1_tens[6]), .f(n5bitadderdisplay_1_tens[5]), .a(n5bitadderdisplay_1_tens[0]),
    .b(n5bitadderdisplay_1_tens[1]), .e(n5bitadderdisplay_1_tens[4]), .d(n5bitadderdisplay_1_tens[3]),
    .c(n5bitadderdisplay_1_tens[2]));  // open: dp
  _7_Segment_Display u_7_segment_display_2 (
    .g(n5bitadderdisplay_1_tens_2[6]), .f(n5bitadderdisplay_1_tens_2[5]), .a(n5bitadderdisplay_1_tens_2[0]),
    .b(n5bitadderdisplay_1_tens_2[1]), .e(n5bitadderdisplay_1_tens_2[4]), .d(n5bitadderdisplay_1_tens_2[3]),
    .c(n5bitadderdisplay_1_tens_2[2]));  // open: dp
endmodule

module _1BitAdder (
  input  A,
  input  B,
  input  Carry_In,
  output C,
  output Carry_Out
);

  wire and_1_out, and_2_out, xor_1_out;

  xor xor_1 (xor_1_out, A, B);
  xor xor_2 (C, xor_1_out, Carry_In);
  and and_1 (and_1_out, xor_1_out, Carry_In);
  and and_2 (and_2_out, A, B);
  or or_1 (Carry_Out, and_1_out, and_2_out);
endmodule

module _5BitAdder (
  input  Carry_In,
  input  [4:0] in_2,
  input  [4:0] in_3,
  output [4:0] C,
  output Carry_Out
);

  wire n1bitadder_1_carry_out, n1bitadder_2_carry_out, n1bitadder_3_carry_out, n1bitadder_4_carry_out;

  _1BitAdder u_1bitadder_1 (
    .A(in_2[0]), .B(in_3[0]), .Carry_In(Carry_In), .C(C[0]), .Carry_Out(n1bitadder_1_carry_out));
  _1BitAdder u_1bitadder_2 (
    .A(in_2[1]), .B(in_3[1]), .Carry_In(n1bitadder_1_carry_out), .C(C[1]), .Carry_Out(n1bitadder_2_carry_out));
  _1BitAdder u_1bitadder_3 (
    .A(in_2[2]), .B(in_3[2]), .Carry_In(n1bitadder_2_carry_out), .C(C[2]), .Carry_Out(n1bitadder_3_carry_out));
  _1BitAdder u_1bitadder_4 (
    .A(in_2[3]), .B(in_3[3]), .Carry_In(n1bitadder_3_carry_out), .C(C[3]), .Carry_Out(n1bitadder_4_carry_out));
  _1BitAdder u_1bitadder_5 (
    .A(in_2[4]), .B(in_3[4]), .Carry_In(n1bitadder_4_carry_out), .C(C[4]), .Carry_Out(Carry_Out));
endmodule

module _7SegmentController (
  input  [3:0] in_1,
  output A,
  output B,
  output C,
  output D,
  output E,
  output F,
  output G
);

  wire and_1_out, and_2_out, and_3_out, and_4_out, and_5_out, and_6_out, and_7_out, and_8_out,
       comparator_1_gt, or_1_out, xor_1_out, xor_2_out, xor_3_out;
  wire [3:0] multiplexer_1_out;

  Comparator #(.width(4), .mode("unsigned")) comparator_1 (
    .a(in_1), .b(4'b1001), .gt(comparator_1_gt));  // open: eq, lt
  Multiplexer #(.width(4)) multiplexer_1 (
    .in0(in_1), .in1(4'b0000), .out(multiplexer_1_out), .sel(comparator_1_gt));  // open: en
  xor xor_1 (xor_1_out, multiplexer_1_out[2], multiplexer_1_out[0]);
  or or_1 (or_1_out, multiplexer_1_out[1], multiplexer_1_out[0]);
  xor xor_2 (xor_2_out, multiplexer_1_out[2], multiplexer_1_out[0]);
  xor xor_3 (xor_3_out, multiplexer_1_out[0], multiplexer_1_out[1]);
  and and_1 (and_1_out, ~multiplexer_1_out[3], ~multiplexer_1_out[1], xor_1_out);  // AND_Gate
  and and_2 (and_2_out, ~multiplexer_1_out[3], multiplexer_1_out[2], multiplexer_1_out[1], multiplexer_1_out[0]);  // AND_Gate
  and and_3 (and_3_out, ~multiplexer_1_out[3], ~multiplexer_1_out[2], or_1_out);  // AND_Gate
  and and_4 (and_4_out, ~multiplexer_1_out[3], multiplexer_1_out[2], multiplexer_1_out[1], multiplexer_1_out[0]);  // AND_Gate
  nand nand_1 (A, ~multiplexer_1_out[3], ~multiplexer_1_out[1], xor_2_out);  // NAND_Gate
  nand nand_2 (B, ~multiplexer_1_out[3], multiplexer_1_out[2], xor_3_out);  // NAND_Gate
  nand nand_3 (C, ~multiplexer_1_out[3], ~multiplexer_1_out[2], multiplexer_1_out[1], ~multiplexer_1_out[0]);  // NAND_Gate
  nor nor_1 (D, and_1_out, and_2_out);
  and and_5 (and_5_out, ~multiplexer_1_out[3], multiplexer_1_out[1], ~multiplexer_1_out[0]);  // AND_Gate
  and and_6 (and_6_out, ~multiplexer_1_out[2], ~multiplexer_1_out[1], ~multiplexer_1_out[0]);  // AND_Gate
  and and_7 (and_7_out, ~multiplexer_1_out[3], ~multiplexer_1_out[2], ~multiplexer_1_out[1]);  // AND_Gate
  and and_8 (and_8_out, ~multiplexer_1_out[3], multiplexer_1_out[2], multiplexer_1_out[1], multiplexer_1_out[0]);  // AND_Gate
  or or_2 (E, and_5_out, and_6_out);
  nor nor_2 (F, and_3_out, and_4_out);
  nor nor_3 (G, and_7_out, and_8_out);
endmodule

module _5BitAdderDisplay (
  input  [4:0] Val,
  input  [4:0] Val_2,
  output [6:0] Tens,
  output [6:0] Tens_2
);

  wire [3:0] bit_extender_1_out, bit_extender_2_out;
  wire [4:0] n5bitadder_1_c;
  wire [5:0] divider_1_out, divider_1_rem;
  wire [5:5] n5bitadder_1_carry_out;

  _5BitAdder u_5bitadder_1 (
    .Carry_In(1'b0), .in_2(Val), .in_3(Val_2), .C(n5bitadder_1_c), .Carry_Out(n5bitadder_1_carry_out[5]));
  Divider #(.width(6)) divider_1 (
    .a({n5bitadder_1_carry_out[5], n5bitadder_1_c}), .b(6'b001010), .out(divider_1_out), .rem(divider_1_rem));  // open: upper
  Bit_Extender #(.in_width(6), .out_width(4), .\type ("input")) bit_extender_1 (
    .in(divider_1_out), .out(bit_extender_1_out));  // open: extend
  Bit_Extender #(.in_width(6), .out_width(4), .\type ("input")) bit_extender_2 (
    .in(divider_1_rem), .out(bit_extender_2_out));  // open: extend
  _7SegmentController u_7segmentcontroller_1 (
    .in_1(bit_extender_1_out), .A(Tens[0]), .B(Tens[1]), .C(Tens[2]), .D(Tens[3]), .E(Tens[4]), .F(Tens[5]),
    .G(Tens[6]));
  _7SegmentController u_7segmentcontroller_2 (
    .in_1(bit_extender_2_out), .A(Tens_2[0]), .B(Tens_2[1]), .C(Tens_2[2]), .D(Tens_2[3]), .E(Tens_2[4]),
    .F(Tens_2[5]), .G(Tens_2[6]));
endmodule
