// Logisim project ClockFinal.circ as structural Verilog: 7 circuits, main circuit 6BitCounter
module main (
  input  Enable
);

  wire Clock_out;
  wire [6:0] clockcontroller_1_am_pm, clockcontroller_1_ones_place_hr, clockcontroller_1_ones_place_min,
       clockcontroller_1_tens_place_hr, clockcontroller_1_tens_place_min;

  Clock Clock (.out(Clock_out));
  ClockController clockcontroller_1 (
    .Enable(Enable), ._1BitClock(Clock_out), .Tens_Place_Min(clockcontroller_1_tens_place_min),
    .Ones_Place_Min(clockcontroller_1_ones_place_min), .AM_PM(clockcontroller_1_am_pm),
    .Tens_Place_Hr(clockcontroller_1_tens_place_hr), .Ones_Place_Hr(clockcontroller_1_ones_place_hr));
  _7_Segment_Display u_7_segment_display_1 (
    .g(clockcontroller_1_ones_place_hr[6]), .f(clockcontroller_1_ones_place_hr[5]),
    .a(clockcontroller_1_ones_place_hr[0]), .b(clockcontroller_1_ones_place_hr[1]),
    .e(clockcontroller_1_ones_place_hr[4]), .d(clockcontroller_1_ones_place_hr[3]),
    .c(clockcontroller_1_ones_place_hr[2]));  // open: dp
  _7_Segment_Display u_7_segment_display_2 (
    .g(clockcontroller_1_tens_place_hr[6]), .f(clockcontroller_1_tens_place_hr[5]),
    .a(clockcontroller_1_tens_place_hr[0]), .b(clockcontroller_1_tens_place_hr[1]),
    .e(clockcontroller_1_tens_place_hr[4]), .d(clockcontroller_1_tens_place_hr[3]),
    .c(clockcontroller_1_tens_place_hr[2]));  // open: dp
  _7_Segment_Display u_7_segment_display_3 (
    .g(clockcontroller_1_ones_place_min[6]), .f(clockcontroller_1_ones_place_min[5]),
    .a(clockcontroller_1_ones_place_min[0]), .b(clockcontroller_1_ones_place_min[1]),
    .e(clockcontroller_1_ones_place_min[4]), .d(clockcontroller_1_ones_place_min[3]),
    .c(clockcontroller_1_ones_place_min[2]));  // open: dp
  _7_Segment_Display u_7_segment_display_4 (
    .g(clockcontroller_1_tens_place_min[6]), .f(clockcontroller_1_tens_place_min[5]),
    .a(clockcontroller_1_tens_place_min[0]), .b(clockcontroller_1_tens_place_min[1]),
    .e(clockcontroller_1_tens_place_min[4]), .d(clockcontroller_1_tens_place_min[3]),
    .c(clockcontroller_1_tens_place_min[2]));  // open: dp
  _7_Segment_Display u_7_segment_display_5 (
    .g(clockcontroller_1_am_pm[6]), .f(clockcontroller_1_am_pm[5]), .a(clockcontroller_1_am_pm[0]),
    .b(clockcontroller_1_am_pm[1]), .e(clockcontroller_1_am_pm[4]), .d(clockcontroller_1_am_pm[3]),
    .c(clockcontroller_1_am_pm[2]));  // open: dp
endmodule

module _6BitCounter (
  input  Clock,
  input  Enable,
  output [5:0] out_3,
  output Increment
);

  wire comparator_1_lt, multiplexer_1_out;
  wire [5:0] d_ff_1_q, n6bitadder_1_out_4;

  Multiplexer multiplexer_1 (.in0(1'b0), .in1(Clock), .out(multiplexer_1_out), .sel(1'b1), .en(Enable));
  _6BitAdder u_6bitadder_1 (.Carry_In(1'b0), .in_2(6'b000001), .in_3(out_3), .out_4(n6bitadder_1_out_4));
  D_Flip_Flop d_ff_1 (
    .clk(multiplexer_1_out), .D(n6bitadder_1_out_4[0]), .Q(d_ff_1_q[0]));  // open: Qn, preset, en, reset
  D_Flip_Flop d_ff_2 (
    .clk(multiplexer_1_out), .D(n6bitadder_1_out_4[1]), .Q(d_ff_1_q[1]));  // open: Qn, preset, en, reset
  D_Flip_Flop d_ff_3 (
    .clk(multiplexer_1_out), .D(n6bitadder_1_out_4[2]), .Q(d_ff_1_q[2]));  // open: Qn, preset, en, reset
  D_Flip_Flop d_ff_4 (
    .clk(multiplexer_1_out), .D(n6bitadder_1_out_4[3]), .Q(d_ff_1_q[3]));  // open: Qn, preset, en, reset
  D_Flip_Flop d_ff_5 (
    .clk(multiplexer_1_out), .D(n6bitadder_1_out_4[4]), .Q(d_ff_1_q[4]));  // open: Qn, preset, en, reset
  D_Flip_Flop d_ff_6 (
    .clk(multiplexer_1_out), .D(n6bitadder_1_out_4[5]), .Q(d_ff_1_q[5]));  // open: Qn, preset, en, reset
  Comparator #(.width(6), .mode("unsigned")) comparator_1 (
    .a(d_ff_1_q), .b(6'b111011), .eq(Increment), .lt(comparator_1_lt));  // open: gt
  Multiplexer #(.width(6), .enable("false")) multiplexer_2 (
    .in0({6{1'b0}}), .in1(d_ff_1_q), .out(out_3), .sel(comparator_1_lt));
endmodule

module _4BitCounter (
  input  Clock,
  input  Enable,
  output [3:0] out_3,
  output Increment
);

  wire and_1_out, comparator_1_eq, comparator_1_gt, comparator_2_lt, multiplexer_1_out, or_1_out, or_2_out;
  wire [3:0] d_ff_1_q, multiplexer_2_out, n4bitadder_1_out_4;

  Multiplexer multiplexer_1 (.in0(1'b0), .in1(Clock), .out(multiplexer_1_out), .sel(1'b1), .en(Enable));
  _4BitAdder u_4bitadder_1 (
    .Carry_In(1'b0), .in_2(4'b0001), .in_3(out_3), .out_4(n4bitadder_1_out_4));  // open: Increment
  D_Flip_Flop d_ff_1 (
    .clk(multiplexer_1_out), .D(n4bitadder_1_out_4[0]), .Q(d_ff_1_q[0]));  // open: Qn, preset, en, reset
  D_Flip_Flop d_ff_2 (
    .clk(multiplexer_1_out), .D(n4bitadder_1_out_4[1]), .Q(d_ff_1_q[1]));  // open: Qn, preset, en, reset
  D_Flip_Flop d_ff_3 (
    .clk(multiplexer_1_out), .D(n4bitadder_1_out_4[2]), .Q(d_ff_1_q[2]));  // open: Qn, preset, en, reset
  D_Flip_Flop d_ff_4 (
    .clk(multiplexer_1_out), .D(n4bitadder_1_out_4[3]), .Q(d_ff_1_q[3]));  // open: Qn, preset, en, reset
  Comparator #(.width(4), .mode("unsigned")) comparator_1 (
    .a(d_ff_1_q), .b(4'b0000), .gt(comparator_1_gt), .eq(comparator_1_eq));  // open: lt
  Comparator #(.width(4), .mode("unsigned")) comparator_2 (
    .a(d_ff_1_q), .b(4'b1100), .eq(Increment), .lt(comparator_2_lt));  // open: gt
  Multiplexer #(.width(4), .enable("false")) multiplexer_2 (
    .in0(4'b0001), .in1(4'b1100), .out(multiplexer_2_out), .sel(or_2_out));
  Multiplexer #(.width(4), .enable("false")) multiplexer_3 (
    .in0(multiplexer_2_out), .in1(d_ff_1_q), .out(out_3), .sel(and_1_out));
  or or_1 (or_1_out, Increment, comparator_2_lt);
  or or_2 (or_2_out, comparator_1_eq, Increment);
  and and_1 (and_1_out, comparator_1_gt, or_1_out);
endmodule

module _4BitAdder (
  input  Carry_In,
  input  [3:0] in_2,
  input  [3:0] in_3,
  output [3:0] out_4,
  output Increment
);

  wire n1bitadder_1_carry_out, n1bitadder_2_carry_out, n1bitadder_3_carry_out;

  _1BitAdder u_1bitadder_1 (
    .A(in_2[0]), .B(in_3[0]), .Carry_In(Carry_In), .C(out_4[0]), .Carry_Out(n1bitadder_1_carry_out));
  _1BitAdder u_1bitadder_2 (
    .A(in_2[1]), .B(in_3[1]), .Carry_In(n1bitadder_1_carry_out), .C(out_4[1]),
    .Carry_Out(n1bitadder_2_carry_out));
  _1BitAdder u_1bitadder_3 (
    .A(in_2[2]), .B(in_3[2]), .Carry_In(n1bitadder_2_carry_out), .C(out_4[2]),
    .Carry_Out(n1bitadder_3_carry_out));
  _1BitAdder u_1bitadder_4 (
    .A(in_2[3]), .B(in_3[3]), .Carry_In(n1bitadder_3_carry_out), .C(out_4[3]), .Carry_Out(Increment));
endmodule

module _1BitAdder (
  input  A,
  input  B,
  input  Carry_In,
  output C,
  output Carry_Out
);

  wire and_1_out, and_2_out, xor_1_out;

  xor xor_1 (xor_1_out, A, B);
  xor xor_2 (C, xor_1_out, Carry_In);
  and and_1 (and_1_out, xor_1_out, Carry_In);
  and and_2 (and_2_out, A, B);
  or or_1 (Carry_Out, and_1_out, and_2_out);
endmodule

module ClockController (
  input  Enable,
  input  _1BitClock,
  output [6:0] Tens_Place_Min,
  output [6:0] Ones_Place_Min,
  output [6:0] AM_PM,
  output [6:0] Tens_Place_Hr,
  output [6:0] Ones_Place_Hr
);

  wire _1BitAdder_carry_out, and_1_out, n4bitcounter_1_increment, n6bitcounter_1_increment,
       n6bitcounter_2_increment;
  wire [3:0] bit_extender_1_out, bit_extender_2_out, divider_2_out, divider_2_rem, n4bitcounter_1_out_3;
  wire [5:0] divider_1_out, divider_1_rem, n6bitcounter_2_out_3;

  _6BitCounter u_6bitcounter_1 (
    .Clock(_1BitClock), .Enable(Enable), .Increment(n6bitcounter_1_increment));  // open: out_3
  _6BitCounter u_6bitcounter_2 (
    .Clock(_1BitClock), .Enable(n6bitcounter_1_increment), .out_3(n6bitcounter_2_out_3),
    .Increment(n6bitcounter_2_increment));
  Divider #(.width(6)) divider_1 (
    .a(n6bitcounter_2_out_3), .b(6'b001010), .out(divider_1_out), .rem(divider_1_rem));  // open: upper
  and and_1 (and_1_out, n6bitcounter_1_increment, n6bitcounter_2_increment);
  Divider #(.width(4)) divider_2 (
    .a(n4bitcounter_1_out_3), .b(4'b1010), .out(divider_2_out), .rem(divider_2_rem));  // open: upper
  Bit_Extender #(.in_width(6), .out_width(4)) bit_extender_1 (.in(divider_1_out), .out(bit_extender_1_out));
  Bit_Extender #(.in_width(6), .out_width(4)) bit_extender_2 (.in(divider_1_rem), .out(bit_extender_2_out));
  _4BitCounter u_4bitcounter_1 (
    .Clock(_1BitClock), .Enable(and_1_out), .out_3(n4bitcounter_1_out_3), .Increment(n4bitcounter_1_increment));
  _1BitAdder _1BitAdder (.A(AM_PM[2]), .B(1'b1), .Carry_In(1'b0), .Carry_Out(_1BitAdder_carry_out));  // open: C
  _7SegmentController _7SegmentController (
    .in_1(bit_extender_1_out), .A(Tens_Place_Min[0]), .B(Tens_Place_Min[1]), .C(Tens_Place_Min[2]),
    .D(Tens_Place_Min[3]), .E(Tens_Place_Min[4]), .F(Tens_Place_Min[5]), .G(Tens_Place_Min[6]));
  _7SegmentController _7SegmentController_2 (
    .in_1(bit_extender_2_out), .A(Ones_Place_Min[0]), .B(Ones_Place_Min[1]), .C(Ones_Place_Min[2]),
    .D(Ones_Place_Min[3]), .E(Ones_Place_Min[4]), .F(Ones_Place_Min[5]), .G(Ones_Place_Min[6]));
  D_Flip_Flop d_ff_1 (
    .clk(n4bitcounter_1_increment), .D(_1BitAdder_carry_out), .Qn(AM_PM[2]));  // open: Q, preset, en, reset
  _7SegmentController _7SegmentController_3 (
    .in_1(divider_2_out), .A(Tens_Place_Hr[0]), .B(Tens_Place_Hr[1]), .C(Tens_Place_Hr[2]),
    .D(Tens_Place_Hr[3]), .E(Tens_Place_Hr[4]), .F(Tens_Place_Hr[5]), .G(Tens_Place_Hr[6]));
  _7SegmentController _7SegmentController_4 (
    .in_1(divider_2_rem), .A(Ones_Place_Hr[0]), .B(Ones_Place_Hr[1]), .C(Ones_Place_Hr[2]),
    .D(Ones_Place_Hr[3]), .E(Ones_Place_Hr[4]), .F(Ones_Place_Hr[5]), .G(Ones_Place_Hr[6]));

  assign {AM_PM[6:3], AM_PM[1:0]} = 6'b111011;
endmodule

module _7SegmentController (
  input  [3:0] in_1,
  output A,
  output B,
  output C,
  output D,
  output E,
  output F,
  output G
);

  wire and_1_out, and_2_out, and_3_out, and_4_out, and_5_out, and_6_out, and_7_out, and_8_out,
       comparator_1_gt, or_1_out, xor_1_out, xor_2_out, xor_3_out;
  wire [3:0] multiplexer_1_out;

  Comparator #(.width(4), .mode("unsigned")) comparator_1 (
    .a(in_1), .b(4'b1001), .gt(comparator_1_gt));  // open: eq, lt
  Multiplexer #(.width(4), .enable("false")) multiplexer_1 (
    .in0(in_1), .in1(4'b0000), .out(multiplexer_1_out), .sel(comparator_1_gt));
  xor xor_1 (xor_1_out, multiplexer_1_out[2], multiplexer_1_out[0]);
  or or_1 (or_1_out, multiplexer_1_out[1], multiplexer_1_out[0]);
  xor xor_2 (xor_2_out, multiplexer_1_out[2], multiplexer_1_out[0]);
  xor xor_3 (xor_3_out, multiplexer_1_out[0], multiplexer_1_out[1]);
  and and_1 (and_1_out, ~multiplexer_1_out[3], ~multiplexer_1_out[1], xor_1_out);  // AND_Gate
  and and_2 (and_2_out, ~multiplexer_1_out[3], multiplexer_1_out[2], multiplexer_1_out[1], multiplexer_1_out[0]);  // AND_Gate
  and and_3 (and_3_out, ~multiplexer_1_out[3], ~multiplexer_1_out[2], or_1_out);  // AND_Gate
  and and_4 (and_4_out, ~multiplexer_1_out[3], multiplexer_1_out[2], multiplexer_1_out[1], multiplexer_1_out[0]);  // AND_Gate
  nand nand_1 (A, ~multiplexer_1_out[3], ~multiplexer_1_out[1], xor_2_out);  // NAND_Gate
  nand nand_2 (B, ~multiplexer_1_out[3], multiplexer_1_out[2], xor_3_out);  // NAND_Gate
  nand nand_3 (C, ~multiplexer_1_out[3], ~multiplexer_1_out[2], multiplexer_1_out[1], ~multiplexer_1_out[0]);  // NAND_Gate
  nor nor_1 (D, and_1_out, and_2_out);
  and and_5 (and_5_out, ~multiplexer_1_out[3], multiplexer_1_out[1], ~multiplexer_1_out[0]);  // AND_Gate
  and and_6 (and_6_out, ~multiplexer_1_out[2], ~multiplexer_1_out[1], ~multiplexer_1_out[0]);  // AND_Gate
  and and_7 (and_7_out, ~multiplexer_1_out[3], ~multiplexer_1_out[2], ~multiplexer_1_out[1]);  // AND_Gate
  and and_8 (and_8_out, ~multiplexer_1_out[3], multiplexer_1_out[2], multiplexer_1_out[1], multiplexer_1_out[0]);  // AND_Gate
  or or_2 (E, and_5_out, and_6_out);
  nor nor_2 (F, and_3_out, and_4_out);
  nor nor_3 (G, and_7_out, and_8_out);
endmodule
