// Logisim project ClockMinutes.circ as structural Verilog: 7 circuits, main circuit main
module main (
  input  Enable
);

  wire Clock_out;
  wire [6:0] minutecounter_1_out_3, minutecounter_1_out_4;

  Clock Clock (.out(Clock_out));
  MinuteCounter minutecounter_1 (
    .in_1(Enable), .in_2(Clock_out), .out_3(minutecounter_1_out_3), .out_4(minutecounter_1_out_4));
  _7_Segment_Display u_7_segment_display_1 (
    .g(minutecounter_1_out_3[6]), .f(minutecounter_1_out_3[5]), .a(minutecounter_1_out_3[0]),
    .b(minutecounter_1_out_3[1]), .e(minutecounter_1_out_3[4]), .d(minutecounter_1_out_3[3]),
    .c(minutecounter_1_out_3[2]));  // open: dp
  _7_Segment_Display u_7_segment_display_2 (
    .g(minutecounter_1_out_4[6]), .f(minutecounter_1_out_4[5]), .a(minutecounter_1_out_4[0]),
    .b(minutecounter_1_out_4[1]), .e(minutecounter_1_out_4[4]), .d(minutecounter_1_out_4[3]),
    .c(minutecounter_1_out_4[2]));  // open: dp
endmodule

module MinuteCounter (
  input  in_1,
  input  in_2,
  output [6:0] out_3,
  output [6:0] out_4
);

  wire n6bitdisplay_1_increment;

  _6BitCounter_6BitDisplay u_6bitdisplay_1 (
    .Enable_Pin(in_1), .Clock_Pin(in_2), .Increment(n6bitdisplay_1_increment));  // open: Tens, Tens_2
  _6BitCounter_6BitDisplay u_6bitdisplay_2 (
    .Enable_Pin(n6bitdisplay_1_increment), .Clock_Pin(in_2), .Tens(out_3), .Tens_2(out_4));  // open: Increment
endmodule

module _6BitDisplay (
  input  Enable_Pin,
  input  Clock_Pin,
  output Increment,
  output [6:0] Tens,
  output [6:0] Tens_2
);

  wire [3:0] bit_extender_1_out, bit_extender_2_out;
  wire [5:0] divider_1_out, divider_1_rem, n6bitcounter_1_out_3;

  _6BitCounter_6BitCounter u_6bitcounter_1 (
    .Enable(Enable_Pin), .Clock(Clock_Pin), .out_3(n6bitcounter_1_out_3), .Increment(Increment));
  Divider #(.width(6)) divider_1 (
    .a(n6bitcounter_1_out_3), .b(6'b001010), .out(divider_1_out), .rem(divider_1_rem));  // open: upper
  Bit_Extender #(.in_width(6), .out_width(4), .\type ("input")) bit_extender_1 (
    .in(divider_1_out), .out(bit_extender_1_out));  // open: extend
  Bit_Extender #(.in_width(6), .out_width(4), .\type ("input")) bit_extender_2 (
    .in(divider_1_rem), .out(bit_extender_2_out));  // open: extend
  _7SegmentController_COPY u_7segmentcontroller_copy_1 (
    .in_1(bit_extender_1_out), .A(Tens[0]), .B(Tens[1]), .C(Tens[2]), .D(Tens[3]), .E(Tens[4]), .F(Tens[5]),
    .G(Tens[6]));
  _7SegmentController_COPY u_7segmentcontroller_copy_2 (
    .in_1(bit_extender_2_out), .A(Tens_2[0]), .B(Tens_2[1]), .C(Tens_2[2]), .D(Tens_2[3]), .E(Tens_2[4]),
    .F(Tens_2[5]), .G(Tens_2[6]));
endmodule

module _6BitCounter (
  input  Enable,
  input  Clock,
  output [5:0] out_3,
  output Increment
);

  wire comparator_1_lt;
  wire [5:0] d_ff_1_q, multiplexer_1_out, n6bitadder_1_out_4;

  Multiplexer #(.width(6)) multiplexer_1 (
    .in0({6{1'b0}}), .in1(6'b000001), .out(multiplexer_1_out), .sel(Enable));  // open: en
  _6BitCounter_6BitAdder u_6bitadder_1 (
    .Carry_In(1'b0), .in_2(multiplexer_1_out), .in_3(out_3), .out_4(n6bitadder_1_out_4));
  D_Flip_Flop d_ff_1 (.clk(Clock), .D(n6bitadder_1_out_4[0]), .Q(d_ff_1_q[0]));  // open: Qn, preset, en, reset
  D_Flip_Flop d_ff_2 (.clk(Clock), .D(n6bitadder_1_out_4[1]), .Q(d_ff_1_q[1]));  // open: Qn, preset, en, reset
  D_Flip_Flop d_ff_3 (.clk(Clock), .D(n6bitadder_1_out_4[2]), .Q(d_ff_1_q[2]));  // open: Qn, preset, en, reset
  D_Flip_Flop d_ff_4 (.clk(Clock), .D(n6bitadder_1_out_4[3]), .Q(d_ff_1_q[3]));  // open: Qn, preset, en, reset
  D_Flip_Flop d_ff_5 (.clk(Clock), .D(n6bitadder_1_out_4[4]), .Q(d_ff_1_q[4]));  // open: Qn, preset, en, reset
  D_Flip_Flop d_ff_6 (.clk(Clock), .D(n6bitadder_1_out_4[5]), .Q(d_ff_1_q[5]));  // open: Qn, preset, en, reset
  Comparator #(.width(6), .mode("unsigned")) comparator_1 (
    .a(d_ff_1_q), .b(6'b111100), .eq(Increment), .lt(comparator_1_lt));  // open: gt
  Multiplexer #(.width(6), .enable("false")) multiplexer_2 (
    .in0({6{1'b0}}), .in1(d_ff_1_q), .out(out_3), .sel(comparator_1_lt));
endmodule

module _6BitAdder (
  input  Carry_In,
  input  [5:0] in_2,
  input  [5:0] in_3,
  output [5:0] out_4
);

  wire n1bitadder_1_carry_out, n1bitadder_2_carry_out, n1bitadder_3_carry_out, n1bitadder_4_carry_out,
       n1bitadder_5_carry_out;

  _1BitAdder u_1bitadder_1 (
    .A(in_2[0]), .B(in_3[0]), .Carry_In(Carry_In), .C(out_4[0]), .Carry_Out(n1bitadder_1_carry_out));
  _1BitAdder u_1bitadder_2 (
    .A(in_2[1]), .B(in_3[1]), .Carry_In(n1bitadder_1_carry_out), .C(out_4[1]),
    .Carry_Out(n1bitadder_2_carry_out));
  _1BitAdder u_1bitadder_3 (
    .A(in_2[2]), .B(in_3[2]), .Carry_In(n1bitadder_2_carry_out), .C(out_4[2]),
    .Carry_Out(n1bitadder_3_carry_out));
  _1BitAdder u_1bitadder_4 (
    .A(in_2[3]), .B(in_3[3]), .Carry_In(n1bitadder_3_carry_out), .C(out_4[3]),
    .Carry_Out(n1bitadder_4_carry_out));
  _1BitAdder u_1bitadder_5 (
    .A(in_2[4]), .B(in_3[4]), .Carry_In(n1bitadder_4_carry_out), .C(out_4[4]),
    .Carry_Out(n1bitadder_5_carry_out));
  _1BitAdder u_1bitadder_6 (
    .A(in_2[5]), .B(in_3[5]), .Carry_In(n1bitadder_5_carry_out), .C(out_4[5]));  // open: Carry_Out
endmodule

module _1BitAdder (
  input  A,
  input  B,
  input  Carry_In,
  output C,
  output Carry_Out
);

  wire and_1_out, and_2_out, xor_1_out;

  xor xor_1 (xor_1_out, A, B);
  xor xor_2 (C, xor_1_out, Carry_In);
  and and_1 (and_1_out, xor_1_out, Carry_In);
  and and_2 (and_2_out, A, B);
  or or_1 (Carry_Out, and_1_out, and_2_out);
endmodule

module _7SegmentController (
  input  [3:0] in_1,
  output A,
  output B,
  output C,
  output D,
  output E,
  output F,
  output G
);

  wire and_1_out, and_2_out, and_3_out, and_4_out, and_5_out, and_6_out, and_7_out, and_8_out,
       comparator_1_gt, or_1_out, xor_1_out, xor_2_out, xor_3_out;
  wire [3:0] multiplexer_1_out;

  Comparator #(.width(4), .mode("unsigned")) comparator_1 (
    .a(in_1), .b(4'b1001), .gt(comparator_1_gt));  // open: eq, lt
  Multiplexer #(.width(4), .enable("false")) multiplexer_1 (
    .in0(in_1), .in1(4'b0000), .out(multiplexer_1_out), .sel(comparator_1_gt));
  xor xor_1 (xor_1_out, multiplexer_1_out[2], multiplexer_1_out[0]);
  or or_1 (or_1_out, multiplexer_1_out[1], multiplexer_1_out[0]);
  xor xor_2 (xor_2_out, multiplexer_1_out[2], multiplexer_1_out[0]);
  xor xor_3 (xor_3_out, multiplexer_1_out[0], multiplexer_1_out[1]);
  and and_1 (and_1_out, ~multiplexer_1_out[3], ~multiplexer_1_out[1], xor_1_out);  // AND_Gate
  and and_2 (and_2_out, ~multiplexer_1_out[3], multiplexer_1_out[2], multiplexer_1_out[1], multiplexer_1_out[0]);  // AND_Gate
  and and_3 (and_3_out, ~multiplexer_1_out[3], ~multiplexer_1_out[2], or_1_out);  // AND_Gate
  and and_4 (and_4_out, ~multiplexer_1_out[3], multiplexer_1_out[2], multiplexer_1_out[1], multiplexer_1_out[0]);  // AND_Gate
  nand nand_1 (A, ~multiplexer_1_out[3], ~multiplexer_1_out[1], xor_2_out);  // NAND_Gate
  nand nand_2 (B, ~multiplexer_1_out[3], multiplexer_1_out[2], xor_3_out);  // NAND_Gate
  nand nand_3 (C, ~multiplexer_1_out[3], ~multiplexer_1_out[2], multiplexer_1_out[1], ~multiplexer_1_out[0]);  // NAND_Gate
  nor nor_1 (D, and_1_out, and_2_out);
  and and_5 (and_5_out, ~multiplexer_1_out[3], multiplexer_1_out[1], ~multiplexer_1_out[0]);  // AND_Gate
  and and_6 (and_6_out, ~multiplexer_1_out[2], ~multiplexer_1_out[1], ~multiplexer_1_out[0]);  // AND_Gate
  and and_7 (and_7_out, ~multiplexer_1_out[3], ~multiplexer_1_out[2], ~multiplexer_1_out[1]);  // AND_Gate
  and and_8 (and_8_out, ~multiplexer_1_out[3], multiplexer_1_out[2], multiplexer_1_out[1], multiplexer_1_out[0]);  // AND_Gate
  or or_2 (E, and_5_out, and_6_out);
  nor nor_2 (F, and_3_out, and_4_out);
  nor nor_3 (G, and_7_out, and_8_out);
endmodule
