// Logisim project CountingCircuit.circ as structural Verilog: 4 circuits, main circuit main
module main (
  input  in_1,
  output [4:0] out_2
);

  wire clock_1_out;

  Clock clock_1 (.out(clock_1_out));
  _5BitCircuit u_5bitcircuit_1 (.Enable(in_1), .Clock(clock_1_out), .out_3(out_2));
endmodule

module _1_Bit_Adder (
  input  A,
  input  B,
  input  Carry_In,
  output C,
  output Carry_Out
);

  wire and_1_out, and_2_out, xor_1_out;

  xor xor_1 (xor_1_out, A, B);
  xor xor_2 (C, xor_1_out, Carry_In);
  and and_1 (and_1_out, xor_1_out, Carry_In);
  and and_2 (and_2_out, A, B);
  or or_1 (Carry_Out, and_1_out, and_2_out);
endmodule

module _5_Bit_Adder (
  input  Carry_In,
  input  [4:0] in_2,
  input  [4:0] in_3,
  output [4:0] out_4
);

  wire n1_bit_adder_1_carry_out, n1_bit_adder_2_carry_out, n1_bit_adder_3_carry_out, n1_bit_adder_4_carry_out;

  _1_Bit_Adder u_1_bit_adder_1 (
    .A(in_2[0]), .B(in_3[0]), .Carry_In(Carry_In), .C(out_4[0]), .Carry_Out(n1_bit_adder_1_carry_out));
  _1_Bit_Adder u_1_bit_adder_2 (
    .A(in_2[1]), .B(in_3[1]), .Carry_In(n1_bit_adder_1_carry_out), .C(out_4[1]),
    .Carry_Out(n1_bit_adder_2_carry_out));
  _1_Bit_Adder u_1_bit_adder_3 (
    .A(in_2[2]), .B(in_3[2]), .Carry_In(n1_bit_adder_2_carry_out), .C(out_4[2]),
    .Carry_Out(n1_bit_adder_3_carry_out));
  _1_Bit_Adder u_1_bit_adder_4 (
    .A(in_2[3]), .B(in_3[3]), .Carry_In(n1_bit_adder_3_carry_out), .C(out_4[3]),
    .Carry_Out(n1_bit_adder_4_carry_out));
  _1_Bit_Adder u_1_bit_adder_5 (
    .A(in_2[4]), .B(in_3[4]), .Carry_In(n1_bit_adder_4_carry_out), .C(out_4[4]));  // open: Carry_Out
endmodule

module _5BitCircuit (
  input  Enable,
  input  Clock,
  output [4:0] out_3
);

  wire [4:0] d_ff_1_q, multiplexer_1_out;

  Multiplexer #(.width(5)) multiplexer_1 (
    .in0({5{1'b0}}), .in1(5'b00001), .out(multiplexer_1_out), .sel(Enable));  // open: en
  _5_Bit_Adder u_5_bit_adder_1 (.Carry_In(1'b0), .in_2(multiplexer_1_out), .in_3(d_ff_1_q), .out_4(out_3));
  D_Flip_Flop d_ff_1 (.clk(Clock), .D(out_3[0]), .Q(d_ff_1_q[0]));  // open: Qn, preset, en, reset
  D_Flip_Flop d_ff_2 (.clk(Clock), .D(out_3[1]), .Q(d_ff_1_q[1]));  // open: Qn, preset, en, reset
  D_Flip_Flop d_ff_3 (.clk(Clock), .D(out_3[2]), .Q(d_ff_1_q[2]));  // open: Qn, preset, en, reset
  D_Flip_Flop d_ff_4 (.clk(Clock), .D(out_3[3]), .Q(d_ff_1_q[3]));  // open: Qn, preset, en, reset
  D_Flip_Flop d_ff_5 (.clk(Clock), .D(out_3[4]), .Q(d_ff_1_q[4]));  // open: Qn, preset, en, reset
endmodule
