// Logisim project FullClock.circ as structural Verilog
module _6BitCounter (
  input  Enable,
  input  Clock,
  output [5:0] out_3,
  output Increment
);

  wire comparator_1_lt;
  wire [5:0] d_ff_1_q, multiplexer_1_out, n6bitadder_1_out_4;

  Multiplexer #(.width(6)) multiplexer_1 (
    .in0({6{1'b0}}), .in1(6'b000001), .out(multiplexer_1_out), .sel(Enable));  // open: en
  _6BitAdder u_6bitadder_1 (.Carry_In(1'b0), .in_2(multiplexer_1_out), .in_3(out_3), .out_4(n6bitadder_1_out_4));
  D_Flip_Flop d_ff_1 (.clk(Clock), .D(n6bitadder_1_out_4[0]), .Q(d_ff_1_q[0]));  // open: Qn, preset, en, reset
  D_Flip_Flop d_ff_2 (.clk(Clock), .D(n6bitadder_1_out_4[1]), .Q(d_ff_1_q[1]));  // open: Qn, preset, en, reset
  D_Flip_Flop d_ff_3 (.clk(Clock), .D(n6bitadder_1_out_4[2]), .Q(d_ff_1_q[2]));  // open: Qn, preset, en, reset
  D_Flip_Flop d_ff_4 (.clk(Clock), .D(n6bitadder_1_out_4[3]), .Q(d_ff_1_q[3]));  // open: Qn, preset, en, reset
  D_Flip_Flop d_ff_5 (.clk(Clock), .D(n6bitadder_1_out_4[4]), .Q(d_ff_1_q[4]));  // open: Qn, preset, en, reset
  D_Flip_Flop d_ff_6 (.clk(Clock), .D(n6bitadder_1_out_4[5]), .Q(d_ff_1_q[5]));  // open: Qn, preset, en, reset
  Comparator #(.width(6), .mode("unsigned")) comparator_1 (
    .a(d_ff_1_q), .b(6'b111100), .eq(Increment), .lt(comparator_1_lt));  // open: gt
  Multiplexer #(.width(6), .enable("false")) multiplexer_2 (
    .in0({6{1'b0}}), .in1(d_ff_1_q), .out(out_3), .sel(comparator_1_lt));
endmodule

module _4BitCounter (
  input  Enable,
  input  Clock,
  output [3:0] out_3,
  output Increment
);

  wire comparator_1_lt;
  wire [3:0] adder_1_out, d_ff_1_q, multiplexer_1_out;

  Multiplexer #(.width(4)) multiplexer_1 (
    .in0(4'b0000), .in1(4'b0001), .out(multiplexer_1_out), .sel(Enable));  // open: en
  Adder #(.width(4)) adder_1 (.a(4'b0000), .b(out_3), .out(adder_1_out));  // open: cin, cout
  D_Flip_Flop d_ff_1 (.clk(Clock), .D(adder_1_out[0]), .Q(d_ff_1_q[0]));  // open: Qn, preset, en, reset
  D_Flip_Flop d_ff_2 (.clk(Clock), .D(adder_1_out[1]), .Q(d_ff_1_q[1]));  // open: Qn, preset, en, reset
  D_Flip_Flop d_ff_3 (.clk(Clock), .D(adder_1_out[2]), .Q(d_ff_1_q[2]));  // open: Qn, preset, en, reset
  D_Flip_Flop d_ff_4 (.clk(Clock), .D(adder_1_out[3]), .Q(d_ff_1_q[3]));  // open: Qn, preset, en, reset
  Comparator #(.width(4), .mode("unsigned")) comparator_1 (
    .a(d_ff_1_q), .b(4'b1100), .eq(Increment), .lt(comparator_1_lt));  // open: gt
  Multiplexer #(.width(4), .enable("false")) multiplexer_2 (
    .in0(4'b0000), .in1(d_ff_1_q), .out(out_3), .sel(comparator_1_lt));
endmodule

module _4BitAdder (
  input  Carry_In,
  input  [3:0] in_2,
  input  [3:0] in_3,
  output [3:0] out_4
);

  wire n1bitadder_1_carry_out, undriven_2, undriven_3;
  wire [5:4] undriven, undriven_4;

  _1BitAdder u_1bitadder_1 (
    .A(undriven_2), .B(undriven_3), .Carry_In(Carry_In), .C(out_4[0]), .Carry_Out(n1bitadder_1_carry_out));
  // Pins of 4 and 6 bits meet at {undriven, in_3}
  // Pins of 4 and 6 bits meet at {undriven_4, out_4}
endmodule

module _1BitAdder (
  input  A,
  input  B,
  input  Carry_In,
  output C,
  output Carry_Out
);

  wire and_1_out, and_2_out, xor_1_out;

  xor xor_1 (xor_1_out, A, B);
  xor xor_2 (C, xor_1_out, Carry_In);
  and and_1 (and_1_out, xor_1_out, Carry_In);
  and and_2 (and_2_out, A, B);
  or or_1 (Carry_Out, and_1_out, and_2_out);
endmodule
