// Logisim project Midterm.circ as structural Verilog: 1 circuit, main circuit main
// A + B means A + B (A OR B)
module main (
  input  A,
  input  B,
  output C,
  output D,
  output E
);

  wire and_1_out, or_1_out, xor_1_out;

  xor xor_1 (xor_1_out, A, B);
  and and_1 (and_1_out, A, B);
  buf or_1 (or_1_out, B);  // OR_Gate
  and and_2 (E, A, B);
  and and_3 (D, A, B);
  buf xor_2 (C, xor_1_out);  // XOR_Gate
  // XOR_Gate xor_3 is placed but not wired

  // Notes on the sheet:
  //   A means (NOT A)
  //   A.B means A * B (A AND B)
  //   A + B means A + B (A OR B)
endmodule
